// Logisim project processor.circ as structural Verilog
module monocycle_processor (
);

  Adder #(.width(32)) adder_1 ();  // open: a, b, out, cin, cout
endmodule

module program_counter (
);

  D_Flip_Flop d_ff_1 ();  // open: D, clk, Q, Qn, preset, reset
  Adder adder_1 ();  // open: a, b, out, cin, cout
endmodule
